// Logisim project schematic1.circ as structural Verilog: 1 circuit, main circuit main
module main (
  input  [31:0] in1,
  input  load,
  input  clk,
  output [31:0] out1
);

  wire [1:0] counter_1_q;
  wire [31:0] adder_1_out, and_1_out, multiplexer_1_out, negator_1_out, negator_2_out, R1_q;

  Register #(.width(32)) R1 (.D(in1), .en(load), .clk(clk), .Q(R1_q));  // open: clr
  Register #(.width(32)) R2 (.D(multiplexer_1_out), .clk(clk), .Q(out1));  // open: en, clr
  Counter #(.max('h3), .width(2)) counter_1 (
    .load(load), .up(1'b1), .count(1'b1), .clk(clk), .D(2'b00), .Q(counter_1_q));  // open: clr, carry
  Negator #(.width(32)) negator_1 (.in(R1_q), .out(negator_1_out));
  assign and_1_out = R1_q & out1;  // AND_Gate and_1, 32 bits wide
  Negator #(.width(32)) negator_2 (.in(out1), .out(negator_2_out));
  Adder #(.width(32)) adder_1 (.a(out1), .b(R1_q), .out(adder_1_out));  // open: cin, cout
  Multiplexer #(.select(2), .width(32)) multiplexer_1 (
    .in0(negator_1_out), .in1(and_1_out), .in2(negator_2_out), .in3(adder_1_out), .out(multiplexer_1_out),
    .sel(counter_1_q));
endmodule
