// Logisim project schematic2.circ as structural Verilog: 1 circuit, main circuit main
module main (
  input  [31:0] divisor,
  input  [31:0] dividend,
  input  start,
  input  clk,
  output [31:0] remainder,
  output [31:0] quotient,
  output done
);

  wire and_1_out, and_2_out, and_3_out, and_4_out, comparator_1_eq, comparator_2_eq, comparator_3_lt,
       nor_1_out, not_1_out, not_2_out, not_3_out, or_1_out, or_2_out, or_3_out, or_5_out, S3_q;
  wire [1:0] S1_q;
  wire [31:0] b_q, counter_q, multiplexer_1_out, multiplexer_2_out, multiplexer_3_out, or_4_out,
       subtractor_1_out, subtractor_2_out;
  wire [63:0] shifter_1_out;

  D_Flip_Flop S1 (.D(start), .clk(clk), .Q(S1_q[0]));  // open: Qn, preset, reset
  Register #(.width(32)) counter (.D(multiplexer_1_out), .en(or_1_out), .clk(clk), .Q(counter_q));  // open: clr
  Multiplexer #(.width(32)) multiplexer_1 (
    .in0(subtractor_1_out), .in1(32'h20), .out(multiplexer_1_out), .sel(S1_q[0]));
  or or_1 (or_1_out, S1_q[0], S1_q[1]);
  Multiplexer #(.select(2), .width(32)) multiplexer_2 (
    .in0(subtractor_2_out), .in1({32{1'b0}}), .in2(shifter_1_out[63:32]), .out(multiplexer_2_out), .sel(S1_q));  // open: in3
  Multiplexer #(.select(2), .width(32)) multiplexer_3 (
    .in0(or_4_out), .in1(dividend), .in2(shifter_1_out[31:0]), .out(multiplexer_3_out), .sel(S1_q));  // open: in3
  nor nor_1 (nor_1_out, comparator_2_eq, not_1_out);
  not not_1 (not_1_out, S3_q);
  or or_2 (or_2_out, S1_q[0], S1_q[1], S3_q);
  Subtractor #(.width(32)) subtractor_1 (.a(counter_q), .b(32'h1), .out(subtractor_1_out));  // open: bin, bout
  Register #(.width(32)) a (.D(multiplexer_2_out), .en(or_2_out), .clk(clk), .Q(remainder), .clr(S1_q[0]));
  Register #(.width(32)) b (.D(divisor), .en(S1_q[0]), .clk(clk), .Q(b_q));  // open: clr
  Register #(.width(32)) q (.D(multiplexer_3_out), .en(or_2_out), .clk(clk), .Q(quotient));  // open: clr
  D_Flip_Flop S2 (.D(or_3_out), .clk(clk), .Q(S1_q[1]), .reset(start));  // open: Qn, preset
  or or_3 (or_3_out, nor_1_out, S1_q[0], and_4_out);
  Comparator #(.width(32)) comparator_1 (.a(subtractor_1_out), .b({32{1'b0}}), .eq(comparator_1_eq));  // open: gt, lt
  Comparator #(.width(32)) comparator_2 (.a(counter_q), .b({32{1'b0}}), .eq(comparator_2_eq));  // open: gt, lt
  assign or_4_out = quotient | 32'h1;  // OR_Gate or_4, 32 bits wide
  D_Flip_Flop S3 (.D(and_3_out), .clk(clk), .Q(S3_q), .reset(start));  // open: Qn, preset
  Subtractor #(.width(32)) subtractor_2 (.a(remainder), .b(b_q), .out(subtractor_2_out));  // open: bin, bout
  and and_1 (and_1_out, comparator_2_eq, S3_q);
  Shifter #(.width(64)) shifter_1 (.in({remainder, quotient}), .\dist (6'b000001), .out(shifter_1_out));
  Comparator #(.width(32)) comparator_3 (.a(remainder), .b(b_q), .lt(comparator_3_lt));  // open: gt, eq
  and and_2 (and_2_out, S1_q[1], comparator_3_lt, comparator_1_eq);
  not not_2 (not_2_out, comparator_3_lt);
  and and_3 (and_3_out, S1_q[1], not_2_out);
  D_Flip_Flop Sd (.D(or_5_out), .clk(clk), .Q(done), .reset(start));  // open: Qn, preset
  or or_5 (or_5_out, done, and_2_out, and_1_out);
  not not_3 (not_3_out, comparator_1_eq);
  and and_4 (and_4_out, not_3_out, comparator_3_lt, S1_q[1]);
endmodule
