// Logisim project schematic.circ as structural Verilog: 1 circuit, main circuit main
module main (
  input  [3:0] a,
  input  [3:0] b,
  input  sub_notadd,
  output [3:0] s,
  output cout
);

  wire adder_1_cout, subtractor_1_bout;
  wire [3:0] adder_1_out, subtractor_1_out;

  Adder #(.width(4)) adder_1 (.a(a), .b(b), .out(adder_1_out), .cout(adder_1_cout));  // open: cin
  Subtractor #(.width(4)) subtractor_1 (.a(a), .b(b), .out(subtractor_1_out), .bout(subtractor_1_bout));  // open: bin
  Multiplexer #(.width(4)) multiplexer_1 (.in0(adder_1_out), .in1(subtractor_1_out), .out(s), .sel(sub_notadd));
  Multiplexer multiplexer_2 (.in0(adder_1_cout), .in1(subtractor_1_bout), .out(cout), .sel(sub_notadd));
endmodule
