// Logisim project schematic.circ as structural Verilog
module main (
  input  [31:0] a,
  input  [31:0] b,
  input  [3:0] aluop,
  input  output_inverted,
  input  output_inc,
  input  rst,
  input  clk,
  output [31:0] res_low,
  output [31:0] res_high,
  output done
);

  wire and_1_out, and_2_out, comparator_1_eq, comparator_2_eq, comparator_3_eq, comparator_4_eq, nand_1_out,
       sub_circ_p4;
  wire [0:0] add_circ_cout;
  wire [31:0] a_t, add_circ_s, and_circ_and_circ, b_t, bit_extender_1_out, div_circ_quotient,
       div_circ_remainder, multiplexer_1_out, multiplexer_2_out, multiplexer_3_out, multiplexer_4_out,
       not_1_out, not_2_out, or_circ_or_circ, sll_circ_sll_circ, srl_sra_rot_out_4, sub_circ_p3,
       xor_circ_xor_circ;

  Register #(.width(32)) register_1 (.D(a), .clk(clk), .Q(a_t), .clr(rst));  // open: en
  Register #(.width(32)) register_2 (.D(b), .clk(clk), .Q(b_t), .clr(rst));  // open: en
  Comparator #(.mode("unsigned"), .width(32)) comparator_1 (.a(a_t), .b(a), .eq(comparator_1_eq));  // open: gt, lt
  Comparator #(.mode("unsigned"), .width(32)) comparator_2 (.a(b_t), .b(b), .eq(comparator_2_eq));  // open: gt, lt
  nand nand_1 (nand_1_out, comparator_1_eq, comparator_2_eq);
  Comparator #(.mode("unsigned"), .width(4)) comparator_3 (
    .a(aluop), .b(4'b0011), .eq(comparator_3_eq));  // open: gt, lt
  Comparator #(.mode("unsigned"), .width(4)) comparator_4 (
    .a(aluop), .b(4'b0100), .eq(comparator_4_eq));  // open: gt, lt
  and and_1 (and_1_out, comparator_3_eq, nand_1_out);
  and and_2 (and_2_out, comparator_4_eq, nand_1_out);
  mul_func mul_circ (.a(a_t), .b(b_t), .start(and_2_out), .clk(clk));
  add_func add_circ (.cin(1'b0), .a(a_t), .b(b_t), .s(add_circ_s), .cout(add_circ_cout[0]));
  // sub_func sub_circ: pin names not known; wires that end beside it: a_t, b_t, sub_circ_p3, sub_circ_p4
  div_func div_circ (
    .divisor(b_t), .dividend(a_t), .start(and_1_out), .clk(clk), .remainder(div_circ_remainder),
    .quotient(div_circ_quotient));  // open: done
  and_func and_circ (.a(a_t), .b(b_t), .and_circ(and_circ_and_circ));
  or_func or_circ (.a(a_t), .b(b_t), .or_circ(or_circ_or_circ));
  xor_func xor_circ (.a(a_t), .b(b_t), .xor_circ(xor_circ_xor_circ));
  sll_func sll_circ (.a(a_t), .b(b_t), .sll_circ(sll_circ_sll_circ));
  srl_func srl_sra_rot (.a(a_t), .aluop(aluop), .b(b_t), .out_4(srl_sra_rot_out_4));
  assign bit_extender_1_out = {{31{sub_circ_p4}}, sub_circ_p4};  // Bit_Extender bit_extender_1
  clz_func clz_func_1 ();
  Multiplexer #(.select(4), .width(32)) multiplexer_1 (
    .in0(add_circ_s), .in1(sub_circ_p3), .in3(div_circ_quotient), .in4(and_circ_and_circ),
    .in5(or_circ_or_circ), .in6(xor_circ_xor_circ), .in9(sll_circ_sll_circ), .in10(srl_sra_rot_out_4),
    .in11(srl_sra_rot_out_4), .in12(srl_sra_rot_out_4), .out(multiplexer_1_out), .sel(aluop));  // open: in2, in7, in8, in13, in14, in15
  Multiplexer #(.select(4), .width(32)) multiplexer_2 (
    .in0({{31{1'b0}}, add_circ_cout[0]}), .in1(bit_extender_1_out), .in3(div_circ_remainder),
    .in4({32{1'b0}}), .in5({32{1'b0}}), .in6({32{1'b0}}), .in7({32{1'b0}}), .in8({32{1'b0}}),
    .in9({32{1'b0}}), .in10({32{1'b0}}), .in11({32{1'b0}}), .in12({32{1'b0}}), .in13({32{1'b0}}),
    .in14({32{1'b0}}), .in15({32{1'b0}}), .out(multiplexer_2_out), .sel(aluop));  // open: in2
  clo_func clo_func_1 ();  // open: in_1, a, res
  assign not_1_out = ~multiplexer_1_out;  // NOT_Gate not_1, 32 bits wide
  assign not_2_out = ~multiplexer_2_out;  // NOT_Gate not_2, 32 bits wide
  Multiplexer #(.width(32)) multiplexer_3 (
    .in0(multiplexer_1_out), .in1(not_1_out), .out(multiplexer_3_out), .sel(output_inverted));
  Multiplexer #(.width(32)) multiplexer_4 (
    .in0(multiplexer_2_out), .in1(not_2_out), .out(multiplexer_4_out), .sel(output_inverted));
  Adder #(.width(32)) adder_1 (.a(multiplexer_3_out), .b({32{1'b0}}), .out(res_low), .cin(output_inc));  // open: cout
  Adder #(.width(32)) adder_2 (.a(multiplexer_4_out), .b({32{1'b0}}), .out(res_high), .cin(output_inc));  // open: cout

  // Other names for the same wires on the sheet: inc = output_inc; invert = output_inverted
endmodule

module and_func (
  input  [31:0] a,
  input  [31:0] b,
  output [31:0] and_circ
);

  assign and_circ = a & b;  // AND_Gate and_1, 32 bits wide
endmodule

module xor_func (
  input  [31:0] a,
  input  [31:0] b,
  output [31:0] xor_circ
);

  assign xor_circ = a ^ b;  // XOR_Gate xor_1, 32 bits wide
endmodule

module or_func (
  input  [31:0] a,
  input  [31:0] b,
  output [31:0] or_circ
);

  assign or_circ = a | b;  // OR_Gate or_1, 32 bits wide
endmodule

module add_func (
  input  cin,
  input  [31:0] a,
  input  [31:0] b,
  output [31:0] s,
  output cout
);

  wire adder_1_cout, adder_2_cout, adder_3_cout, adder_4_cout, adder_5_cout, adder_6_cout, adder_7_cout,
       adder_8_cout, adder_9_cout, adder_10_cout, adder_11_cout, adder_12_cout, adder_13_cout, adder_14_cout,
       adder_15_cout, multiplexer_2_out, multiplexer_4_out, multiplexer_6_out, multiplexer_8_out,
       multiplexer_10_out, multiplexer_12_out;
  wire [3:0] adder_2_out, adder_3_out, adder_4_out, adder_5_out, adder_6_out, adder_7_out, adder_8_out,
       adder_9_out, adder_10_out, adder_11_out, adder_12_out, adder_13_out, adder_14_out, adder_15_out;

  Adder #(.width(4)) adder_1 (.a(a[3:0]), .b(b[3:0]), .out(s[3:0]), .cin(cin), .cout(adder_1_cout));
  Adder #(.width(4)) adder_2 (.a(a[7:4]), .b(b[7:4]), .out(adder_2_out), .cin(1'b0), .cout(adder_2_cout));
  Adder #(.width(4)) adder_3 (.a(a[7:4]), .b(b[7:4]), .out(adder_3_out), .cin(1'b1), .cout(adder_3_cout));
  Adder #(.width(4)) adder_4 (.a(a[11:8]), .b(b[11:8]), .out(adder_4_out), .cin(1'b0), .cout(adder_4_cout));
  Adder #(.width(4)) adder_5 (.a(a[11:8]), .b(b[11:8]), .out(adder_5_out), .cin(1'b1), .cout(adder_5_cout));
  Adder #(.width(4)) adder_6 (.a(a[15:12]), .b(b[15:12]), .out(adder_6_out), .cin(1'b0), .cout(adder_6_cout));
  Adder #(.width(4)) adder_7 (.a(a[15:12]), .b(b[15:12]), .out(adder_7_out), .cin(1'b1), .cout(adder_7_cout));
  Adder #(.width(4)) adder_8 (.a(a[19:16]), .b(b[19:16]), .out(adder_8_out), .cin(1'b0), .cout(adder_8_cout));
  Adder #(.width(4)) adder_9 (.a(a[19:16]), .b(b[19:16]), .out(adder_9_out), .cin(1'b1), .cout(adder_9_cout));
  Adder #(.width(4)) adder_10 (.a(a[23:20]), .b(b[23:20]), .out(adder_10_out), .cin(1'b0), .cout(adder_10_cout));
  Adder #(.width(4)) adder_11 (.a(a[23:20]), .b(b[23:20]), .out(adder_11_out), .cin(1'b1), .cout(adder_11_cout));
  Adder #(.width(4)) adder_12 (.a(a[27:24]), .b(b[27:24]), .out(adder_12_out), .cin(1'b0), .cout(adder_12_cout));
  Adder #(.width(4)) adder_13 (.a(a[27:24]), .b(b[27:24]), .out(adder_13_out), .cin(1'b1), .cout(adder_13_cout));
  Adder #(.width(4)) adder_14 (.a(a[31:28]), .b(b[31:28]), .out(adder_14_out), .cin(1'b0), .cout(adder_14_cout));
  Adder #(.width(4)) adder_15 (.a(a[31:28]), .b(b[31:28]), .out(adder_15_out), .cin(1'b1), .cout(adder_15_cout));
  Multiplexer #(.width(4)) multiplexer_1 (.in0(adder_2_out), .in1(adder_3_out), .out(s[7:4]), .sel(adder_1_cout));
  Multiplexer multiplexer_2 (.in0(adder_2_cout), .in1(adder_3_cout), .out(multiplexer_2_out), .sel(adder_1_cout));
  Multiplexer #(.width(4)) multiplexer_3 (.in0(adder_4_out), .in1(adder_5_out), .out(s[11:8]), .sel(multiplexer_2_out));
  Multiplexer multiplexer_4 (.in0(adder_4_cout), .in1(adder_5_cout), .out(multiplexer_4_out), .sel(multiplexer_2_out));
  Multiplexer #(.width(4)) multiplexer_5 (
    .in0(adder_6_out), .in1(adder_7_out), .out(s[15:12]), .sel(multiplexer_4_out));
  Multiplexer multiplexer_6 (.in0(adder_6_cout), .in1(adder_7_cout), .out(multiplexer_6_out), .sel(multiplexer_4_out));
  Multiplexer #(.width(4)) multiplexer_7 (
    .in0(adder_8_out), .in1(adder_9_out), .out(s[19:16]), .sel(multiplexer_6_out));
  Multiplexer multiplexer_8 (.in0(adder_8_cout), .in1(adder_9_cout), .out(multiplexer_8_out), .sel(multiplexer_6_out));
  Multiplexer #(.width(4)) multiplexer_9 (
    .in0(adder_10_out), .in1(adder_11_out), .out(s[23:20]), .sel(multiplexer_8_out));
  Multiplexer multiplexer_10 (
    .in0(adder_10_cout), .in1(adder_11_cout), .out(multiplexer_10_out), .sel(multiplexer_8_out));
  Multiplexer #(.width(4)) multiplexer_11 (
    .in0(adder_12_out), .in1(adder_13_out), .out(s[27:24]), .sel(multiplexer_10_out));
  Multiplexer multiplexer_12 (
    .in0(adder_12_cout), .in1(adder_13_cout), .out(multiplexer_12_out), .sel(multiplexer_10_out));
  Multiplexer #(.width(4)) multiplexer_13 (
    .in0(adder_14_out), .in1(adder_15_out), .out(s[31:28]), .sel(multiplexer_12_out));
  Multiplexer multiplexer_14 (.in0(adder_14_cout), .in1(adder_15_cout), .out(cout), .sel(multiplexer_12_out));
endmodule

module sub_func (
  input  [31:0] a,
  input  [31:0] b,
  output [31:0] sub_circ,
  output borrow
);

  wire add_func_1_cout;
  wire [31:0] not_1_out;

  assign not_1_out = ~b;  // NOT_Gate not_1, 32 bits wide
  add_func add_func_1 (.cin(1'b1), .a(a), .b(not_1_out), .s(sub_circ), .cout(add_func_1_cout));
  not not_2 (borrow, add_func_1_cout);
endmodule

module mul_func (
  input  [31:0] a,
  input  [31:0] b,
  input  start,
  input  clk
);
endmodule

module div_func (
  input  [31:0] divisor,
  input  [31:0] dividend,
  input  start,
  input  clk,
  output [31:0] remainder,
  output [31:0] quotient,
  output done
);

  wire and_1_out, and_2_out, and_3_out, and_4_out, comparator_1_eq, comparator_2_eq, comparator_3_lt,
       nor_1_out, not_1_out, not_2_out, not_3_out, or_1_out, or_2_out, or_3_out, or_5_out, S3_q;
  wire [1:0] S1_q;
  wire [31:0] b_q, counter_q, multiplexer_1_out, multiplexer_2_out, multiplexer_3_out, or_4_out,
       subtractor_1_out, subtractor_2_out;
  wire [63:0] shifter_1_out;

  D_Flip_Flop S1 (.D(start), .clk(clk), .Q(S1_q[0]));  // open: Qn, preset, reset
  Register #(.width(32)) counter (.D(multiplexer_1_out), .en(or_1_out), .clk(clk), .Q(counter_q));  // open: clr
  Multiplexer #(.width(32)) multiplexer_1 (
    .in0(subtractor_1_out), .in1(32'h20), .out(multiplexer_1_out), .sel(S1_q[0]));
  or or_1 (or_1_out, S1_q[0], S1_q[1]);
  Multiplexer #(.select(2), .width(32)) multiplexer_2 (
    .in0(subtractor_2_out), .in1({32{1'b0}}), .in2(shifter_1_out[63:32]), .out(multiplexer_2_out), .sel(S1_q));  // open: in3
  Multiplexer #(.select(2), .width(32)) multiplexer_3 (
    .in0(or_4_out), .in1(dividend), .in2(shifter_1_out[31:0]), .out(multiplexer_3_out), .sel(S1_q));  // open: in3
  not not_1 (not_1_out, S3_q);
  or or_2 (or_2_out, S1_q[0], S1_q[1], S3_q);
  nor nor_1 (nor_1_out, comparator_2_eq, not_1_out);
  Subtractor #(.width(32)) subtractor_1 (.a(counter_q), .b(32'h1), .out(subtractor_1_out));  // open: bin, bout
  Register #(.width(32)) a (.D(multiplexer_2_out), .en(or_2_out), .clk(clk), .Q(remainder), .clr(S1_q[0]));
  Register #(.width(32)) b (.D(divisor), .en(S1_q[0]), .clk(clk), .Q(b_q));  // open: clr
  Register #(.width(32)) q (.D(multiplexer_3_out), .en(or_2_out), .clk(clk), .Q(quotient));  // open: clr
  D_Flip_Flop S2 (.D(or_3_out), .clk(clk), .Q(S1_q[1]), .reset(start));  // open: Qn, preset
  or or_3 (or_3_out, nor_1_out, S1_q[0], and_4_out);
  Comparator #(.mode("unsigned"), .width(32)) comparator_1 (
    .a(subtractor_1_out), .b({32{1'b0}}), .eq(comparator_1_eq));  // open: gt, lt
  Comparator #(.mode("unsigned"), .width(32)) comparator_2 (
    .a(counter_q), .b({32{1'b0}}), .eq(comparator_2_eq));  // open: gt, lt
  assign or_4_out = quotient | 32'h1;  // OR_Gate or_4, 32 bits wide
  D_Flip_Flop S3 (.D(and_3_out), .clk(clk), .Q(S3_q), .reset(start));  // open: Qn, preset
  Subtractor #(.width(32)) subtractor_2 (.a(remainder), .b(b_q), .out(subtractor_2_out));  // open: bin, bout
  and and_1 (and_1_out, comparator_2_eq, S3_q);
  Shifter #(.width(64)) shifter_1 (.in({remainder, quotient}), .\dist (6'b000001), .out(shifter_1_out));
  Comparator #(.mode("unsigned"), .width(32)) comparator_3 (
    .a(shifter_1_out[63:32]), .b(b_q), .lt(comparator_3_lt));  // open: gt, eq
  and and_2 (and_2_out, S1_q[1], comparator_3_lt, comparator_1_eq);
  not not_2 (not_2_out, comparator_3_lt);
  and and_3 (and_3_out, S1_q[1], not_2_out);
  D_Flip_Flop Sd (.D(or_5_out), .clk(clk), .Q(done), .reset(start));  // open: Qn, preset
  or or_5 (or_5_out, done, and_2_out, and_1_out);
  not not_3 (not_3_out, comparator_1_eq);
  and and_4 (and_4_out, not_3_out, comparator_3_lt, S1_q[1]);
endmodule

module clo_func (
  input  [3:0] in_1,
  input  [31:0] a,
  output [31:0] res
);

  wire multiplexer_1_out, or_2_out, or_3_out, or_4_out, or_5_out, or_6_out, or_7_out, or_8_out;
  wire [1:0] undriven;
  wire [31:0] controlled_inverter_1_out;

  assign controlled_inverter_1_out = in_1[0] ? ~a : 32'bz;  // Controlled_Inverter controlled_inverter_1
  // OR_Gate or_1 has open pins: in0=controlled_inverter_1_out[0], in1=controlled_inverter_1_out[1], in2=controlled_inverter_1_out[2], in3=controlled_inverter_1_out[3], in4=controlled_inverter_1_out[4], in5=controlled_inverter_1_out[5], in6=controlled_inverter_1_out[6], in7=controlled_inverter_1_out[7], in8=controlled_inverter_1_out[8], in9=controlled_inverter_1_out[9], in10=controlled_inverter_1_out[10], in11=controlled_inverter_1_out[11], in12=controlled_inverter_1_out[12], in13=controlled_inverter_1_out[13], in14=controlled_inverter_1_out[14], in15=controlled_inverter_1_out[15], out=open
  or or_2 (or_2_out, controlled_inverter_1_out[16], controlled_inverter_1_out[17], controlled_inverter_1_out[18], controlled_inverter_1_out[19], controlled_inverter_1_out[20], controlled_inverter_1_out[21], controlled_inverter_1_out[22], controlled_inverter_1_out[23], controlled_inverter_1_out[24], controlled_inverter_1_out[25], controlled_inverter_1_out[26], controlled_inverter_1_out[27], controlled_inverter_1_out[28], controlled_inverter_1_out[29], controlled_inverter_1_out[30], controlled_inverter_1_out[31]);
  or or_3 (or_3_out, controlled_inverter_1_out[8], controlled_inverter_1_out[9], controlled_inverter_1_out[10], controlled_inverter_1_out[11], controlled_inverter_1_out[12], controlled_inverter_1_out[13], controlled_inverter_1_out[14], controlled_inverter_1_out[15]);
  or or_4 (or_4_out, controlled_inverter_1_out[24], controlled_inverter_1_out[25], controlled_inverter_1_out[26], controlled_inverter_1_out[27], controlled_inverter_1_out[28], controlled_inverter_1_out[29], controlled_inverter_1_out[30], controlled_inverter_1_out[31]);
  or or_5 (or_5_out, controlled_inverter_1_out[4], controlled_inverter_1_out[5], controlled_inverter_1_out[6], controlled_inverter_1_out[7]);
  or or_6 (or_6_out, controlled_inverter_1_out[12], controlled_inverter_1_out[13], controlled_inverter_1_out[14], controlled_inverter_1_out[15]);
  or or_7 (or_7_out, controlled_inverter_1_out[20], controlled_inverter_1_out[21], controlled_inverter_1_out[22], controlled_inverter_1_out[23]);
  or or_8 (or_8_out, controlled_inverter_1_out[28], controlled_inverter_1_out[29], controlled_inverter_1_out[30], controlled_inverter_1_out[31]);
  // OR_Gate or_9 has open pins: in0=controlled_inverter_1_out[2], in1=controlled_inverter_1_out[3], out=open
  // OR_Gate or_10 has open pins: in0=controlled_inverter_1_out[6], in1=controlled_inverter_1_out[7], out=open
  // OR_Gate or_11 has open pins: in0=controlled_inverter_1_out[10], in1=controlled_inverter_1_out[11], out=open
  // OR_Gate or_12 has open pins: in0=controlled_inverter_1_out[14], in1=controlled_inverter_1_out[15], out=open
  // OR_Gate or_13 has open pins: in0=controlled_inverter_1_out[18], in1=controlled_inverter_1_out[19], out=open
  // OR_Gate or_14 has open pins: in0=controlled_inverter_1_out[22], in1=controlled_inverter_1_out[23], out=open
  // OR_Gate or_15 has open pins: in0=controlled_inverter_1_out[26], in1=controlled_inverter_1_out[27], out=open
  // OR_Gate or_16 has open pins: in0=controlled_inverter_1_out[30], in1=controlled_inverter_1_out[31], out=open
  // OR_Gate or_17 is placed but not wired
  Multiplexer multiplexer_1 (.in0(or_3_out), .in1(or_4_out), .out(multiplexer_1_out), .sel(or_2_out));
  Multiplexer #(.select(2)) multiplexer_2 (
    .in0(or_5_out), .in1(or_6_out), .in2(or_7_out), .in3(or_8_out), .sel(undriven));  // open: out
endmodule

module sll_func (
  input  [31:0] a,
  input  [31:0] b,
  output [31:0] sll_circ
);

  wire [31:0] multiplexer_1_out, multiplexer_2_out, multiplexer_3_out, multiplexer_4_out;

  Multiplexer #(.width(32)) multiplexer_1 (.in0(a), .in1({a[30:0], 1'b0}), .out(multiplexer_1_out), .sel(b[0]));
  Multiplexer #(.width(32)) multiplexer_2 (
    .in0(multiplexer_1_out), .in1({multiplexer_1_out[29:0], 2'b00}), .out(multiplexer_2_out), .sel(b[1]));
  Multiplexer #(.width(32)) multiplexer_3 (
    .in0(multiplexer_2_out), .in1({multiplexer_2_out[27:0], 4'b0000}), .out(multiplexer_3_out), .sel(b[2]));
  Multiplexer #(.width(32)) multiplexer_4 (
    .in0(multiplexer_3_out), .in1({multiplexer_3_out[23:0], {8{1'b0}}}), .out(multiplexer_4_out), .sel(b[3]));
  Multiplexer #(.width(32)) multiplexer_5 (
    .in0(multiplexer_4_out), .in1({multiplexer_4_out[15:0], {16{1'b0}}}), .out(sll_circ), .sel(b[4]));
endmodule

module srl_func (
  input  [31:0] a,
  input  [3:0] aluop,
  input  [31:0] b,
  output [31:0] out_4
);

  wire [1:0] bit_extender_1_out, multiplexer_2_out_2, multiplexer_3_out;
  wire [3:0] bit_extender_2_out, multiplexer_4_out, multiplexer_5_out;
  wire [7:0] bit_extender_3_out, multiplexer_6_out_2, multiplexer_7_out;
  wire [15:0] bit_extender_4_out, multiplexer_9_out;
  wire [23:0] multiplexer_6_out;
  wire [27:0] multiplexer_4_out_2;
  wire [29:0] multiplexer_2_out;
  wire [31:0] multiplexer_8_out;
  wire [31:31] multiplexer_1_out;

  Multiplexer #(.select(2)) multiplexer_1 (
    .in0(1'b0), .in1(a[31]), .in2(a[0]), .out(multiplexer_1_out[31]), .sel({aluop[2], aluop[0]}));  // open: in3
  Multiplexer #(.width(32)) multiplexer_2 (
    .in0(a), .in1({multiplexer_1_out[31], a[31:1]}), .out({multiplexer_2_out, multiplexer_2_out_2}),
    .sel(b[0]));
  assign bit_extender_1_out = {{1{multiplexer_2_out[29]}}, multiplexer_2_out[29]};  // Bit_Extender bit_extender_1
  Multiplexer #(.select(2), .width(2)) multiplexer_3 (
    .in0(2'b00), .in1(bit_extender_1_out), .in2(multiplexer_2_out_2), .out(multiplexer_3_out),
    .sel({aluop[2], aluop[0]}));  // open: in3
  Multiplexer #(.width(32)) multiplexer_4 (
    .in0({multiplexer_2_out, multiplexer_2_out_2}), .in1({multiplexer_3_out, multiplexer_2_out}),
    .out({multiplexer_4_out_2, multiplexer_4_out}), .sel(b[1]));
  assign bit_extender_2_out = {{3{multiplexer_4_out_2[27]}}, multiplexer_4_out_2[27]};  // Bit_Extender bit_extender_2
  Multiplexer #(.select(2), .width(4)) multiplexer_5 (
    .in0(4'b0000), .in1(bit_extender_2_out), .in2(multiplexer_4_out), .out(multiplexer_5_out),
    .sel({aluop[2], aluop[0]}));  // open: in3
  Multiplexer #(.width(32)) multiplexer_6 (
    .in0({multiplexer_4_out_2, multiplexer_4_out}), .in1({multiplexer_5_out, multiplexer_4_out_2}),
    .out({multiplexer_6_out, multiplexer_6_out_2}), .sel(b[2]));
  assign bit_extender_3_out = {{7{multiplexer_6_out[23]}}, multiplexer_6_out[23]};  // Bit_Extender bit_extender_3
  Multiplexer #(.select(2), .width(8)) multiplexer_7 (
    .in0({8{1'b0}}), .in1(bit_extender_3_out), .in2(multiplexer_6_out_2), .out(multiplexer_7_out),
    .sel({aluop[2], aluop[0]}));  // open: in3
  Multiplexer #(.width(32)) multiplexer_8 (
    .in0({multiplexer_6_out, multiplexer_6_out_2}), .in1({multiplexer_7_out, multiplexer_6_out}),
    .out(multiplexer_8_out), .sel(b[3]));
  assign bit_extender_4_out = {{15{multiplexer_8_out[31]}}, multiplexer_8_out[31]};  // Bit_Extender bit_extender_4
  Multiplexer #(.select(2), .width(16)) multiplexer_9 (
    .in0({16{1'b0}}), .in1(bit_extender_4_out), .in2(multiplexer_8_out[15:0]), .out(multiplexer_9_out),
    .sel({aluop[2], aluop[0]}));  // open: in3
  Multiplexer #(.width(32)) multiplexer_10 (
    .in0(multiplexer_8_out), .in1({multiplexer_9_out, multiplexer_8_out[31:16]}), .out(out_4), .sel(b[4]));
endmodule
