// Logisim project schematic.circ as structural Verilog: 15 circuits, main circuit main
module main (
  input  clk,
  input  Jen,
  input  [31:0] Jin,
  input  rst,
  output [31:0] Jout,
  output [31:0] R1,
  output [31:0] R2,
  output [31:0] R3,
  output [31:0] R4,
  output [31:0] R5,
  output [31:0] R6,
  output [31:0] R7,
  output [31:0] R8,
  output [31:0] R9,
  output [31:0] R10,
  output [31:0] R11,
  output [31:0] R12,
  output [31:0] R13,
  output [31:0] R14,
  output [31:0] R15,
  output [31:0] R16,
  output [31:0] R17,
  output [31:0] R18,
  output [31:0] R19,
  output [31:0] R20,
  output [31:0] R21,
  output [31:0] R22,
  output [31:0] R23,
  output [31:0] R24,
  output [31:0] R25,
  output [31:0] R26,
  output [31:0] R27,
  output [31:0] R28,
  output [31:0] R29,
  output [31:0] R30,
  output [31:0] R31
);

  wire ALUsrc, MemtoReg, MemWrite, REGdst, RegWrite;
  wire [1:0] ALUop;
  wire [3:0] ALU_controller_alo_control_signal;
  wire [4:0] bit_extender_1_out, multiplexer_1_out, multiplexer_2_out;
  wire [8:0] adder_1_out, PC_q;
  wire [31:0] ALU_UNIT_res, bit_extender_2_out, Dmem_dout, Imem_dout, Jout_t, multiplexer_3_out,
       multiplexer_4_out, Register_File_dread0, Register_File_dread1;

  Register #(.width(9)) PC (.D(adder_1_out), .en(1'b1), .clk(clk), .Q(PC_q), .clr(rst));
  Adder #(.width(9)) adder_1 (.a(PC_q), .b(9'h1), .out(adder_1_out));  // open: cin, cout
  jtag_ram512 Imem (.clk(clk), .Jen(Jen), .Jin(Jin), .Addr(PC_q), .Jout(Jout_t), .Dout(Imem_dout));  // open: Din, Wen
  assign bit_extender_1_out = {{4{1'b0}}, 1'b0};  // Bit_Extender bit_extender_1
  Multiplexer #(.width(5)) multiplexer_1 (
    .in0(Imem_dout[20:16]), .in1(Imem_dout[15:11]), .out(multiplexer_1_out), .sel(REGdst));
  assign bit_extender_2_out = {{16{Imem_dout[15]}}, Imem_dout[15:0]};  // Bit_Extender bit_extender_2
  CU Main_Control (
    .opcode(Imem_dout[31:26]), .MemtoReg(MemtoReg), .REGdst(REGdst), .ALUsrc(ALUsrc), .ALUop(ALUop),
    .RegWrite(RegWrite));
  Multiplexer #(.width(5)) multiplexer_2 (
    .in0(bit_extender_1_out), .in1(multiplexer_1_out), .out(multiplexer_2_out), .sel(RegWrite));
  regfile Register_File (
    .clk(clk), .rst(rst), .Dwrite(multiplexer_4_out), .Awrite(multiplexer_2_out), .Aread0(Imem_dout[25:21]),
    .Aread1(Imem_dout[20:16]), .Dread0(Register_File_dread0), .Dread1(Register_File_dread1), .R1(R1),
    .R2(R2), .R3(R3), .R4(R4), .R5(R5), .R6(R6), .R7(R7), .R8(R8), .R9(R9), .R10(R10), .R11(R11), .R12(R12),
    .R13(R13), .R14(R14), .R15(R15), .R16(R16), .R17(R17), .R18(R18), .R19(R19), .R20(R20), .R21(R21),
    .R22(R22), .R23(R23), .R24(R24), .R25(R25), .R26(R26), .R27(R27), .R28(R28), .R29(R29), .R30(R30),
    .R31(R31));
  Multiplexer #(.width(32)) multiplexer_3 (
    .in0(Register_File_dread1), .in1(bit_extender_2_out), .out(multiplexer_3_out), .sel(ALUsrc));
  ALU_CNT ALU_controller (.aluop(ALUop), .func(Imem_dout[5:0]), .alo_control_signal(ALU_controller_alo_control_signal));
  alu ALU_UNIT (
    .a(Register_File_dread0), .b(multiplexer_3_out), .aluop(ALU_controller_alo_control_signal),
    .res(ALU_UNIT_res));
  jtag_ram512 Dmem (
    .clk(clk), .Jen(Jen), .Din(Register_File_dread1), .Jin(Jout_t), .Wen(MemWrite), .Addr(ALU_UNIT_res[8:0]),
    .Jout(Jout), .Dout(Dmem_dout));
  Multiplexer #(.width(32)) multiplexer_4 (
    .in0(ALU_UNIT_res), .in1(Dmem_dout), .out(multiplexer_4_out), .sel(MemtoReg));
endmodule

module regfile (
  input  clk,
  input  rst,
  input  [31:0] Dwrite,
  input  [4:0] Awrite,
  input  [4:0] Aread0,
  input  [4:0] Aread1,
  output [31:0] Dread0,
  output [31:0] Dread1,
  output [31:0] R1,
  output [31:0] R2,
  output [31:0] R3,
  output [31:0] R4,
  output [31:0] R5,
  output [31:0] R6,
  output [31:0] R7,
  output [31:0] R8,
  output [31:0] R9,
  output [31:0] R10,
  output [31:0] R11,
  output [31:0] R12,
  output [31:0] R13,
  output [31:0] R14,
  output [31:0] R15,
  output [31:0] R16,
  output [31:0] R17,
  output [31:0] R18,
  output [31:0] R19,
  output [31:0] R20,
  output [31:0] R21,
  output [31:0] R22,
  output [31:0] R23,
  output [31:0] R24,
  output [31:0] R25,
  output [31:0] R26,
  output [31:0] R27,
  output [31:0] R28,
  output [31:0] R29,
  output [31:0] R30,
  output [31:0] R31
);

  wire and_1_out, and_2_out, and_3_out, and_4_out, and_5_out, and_6_out, and_7_out, and_8_out, and_9_out,
       and_10_out, and_11_out, and_12_out, and_13_out, and_14_out, and_15_out, and_16_out, and_17_out,
       and_18_out, and_19_out, and_20_out, and_21_out, and_22_out, and_23_out, and_24_out, and_25_out,
       and_26_out, and_27_out, and_28_out, and_29_out, and_30_out, and_31_out, and_32_out, decoder_1_out0,
       decoder_1_out1, decoder_1_out2, decoder_1_out3, decoder_1_out4, decoder_1_out5, decoder_1_out6,
       decoder_1_out7, decoder_2_out0, decoder_2_out1, decoder_2_out2, decoder_2_out3, or_1_out, or_2_out,
       or_3_out, or_4_out, or_5_out, or_6_out, or_7_out, or_8_out, or_9_out, or_10_out, or_11_out, or_12_out,
       or_13_out, or_14_out, or_15_out, or_16_out, or_17_out, or_18_out, or_19_out, or_20_out, or_21_out,
       or_22_out, or_23_out, or_24_out, or_25_out, or_26_out, or_27_out, or_28_out, or_29_out, or_30_out,
       or_31_out, or_32_out, undriven_2, undriven_3, undriven_4, undriven_5;
  wire [31:0] multiplexer_1_out, multiplexer_2_out, multiplexer_3_out, multiplexer_4_out, multiplexer_5_out,
       multiplexer_6_out, multiplexer_7_out, multiplexer_8_out, multiplexer_9_out, undriven;

  Register #(.width(32)) register_1 (.D(undriven), .en(or_1_out), .clk(undriven_2));  // open: Q, clr
  or or_1 (or_1_out, undriven_5, and_1_out);
  and and_1 (and_1_out, undriven_4, undriven_3);
  Decoder #(.select(3)) decoder_1 (
    .out0(decoder_1_out0), .out1(decoder_1_out1), .out2(decoder_1_out2), .out3(decoder_1_out3),
    .out4(decoder_1_out4), .out5(decoder_1_out5), .out6(decoder_1_out6), .out7(decoder_1_out7),
    .sel(Awrite[4:2]));  // open: en
  Decoder #(.select(2)) decoder_2 (
    .out0(decoder_2_out0), .out1(decoder_2_out1), .out2(decoder_2_out2), .out3(decoder_2_out3),
    .sel(Awrite[1:0]));  // open: en
  Multiplexer #(.width(32)) multiplexer_1 (.in0(Dwrite), .in1({32{1'b0}}), .out(multiplexer_1_out), .sel(rst));
  and and_2 (and_2_out, decoder_2_out0, decoder_1_out1);
  and and_3 (and_3_out, decoder_2_out0, decoder_1_out2);
  and and_4 (and_4_out, decoder_2_out0, decoder_1_out3);
  and and_5 (and_5_out, decoder_2_out0, decoder_1_out4);
  and and_6 (and_6_out, decoder_2_out0, decoder_1_out5);
  and and_7 (and_7_out, decoder_2_out0, decoder_1_out6);
  and and_8 (and_8_out, decoder_2_out0, decoder_1_out7);
  Register #(.width(32)) register_2 (.D(multiplexer_1_out), .en(or_2_out), .clk(clk), .Q(R4));  // open: clr
  or or_2 (or_2_out, rst, and_2_out);
  Register #(.width(32)) register_3 (.D(multiplexer_1_out), .en(or_3_out), .clk(clk), .Q(R8));  // open: clr
  or or_3 (or_3_out, rst, and_3_out);
  Register #(.width(32)) register_4 (.D(multiplexer_1_out), .en(or_4_out), .clk(clk), .Q(R12));  // open: clr
  or or_4 (or_4_out, rst, and_4_out);
  Register #(.width(32)) register_5 (.D(multiplexer_1_out), .en(or_5_out), .clk(clk), .Q(R16));  // open: clr
  or or_5 (or_5_out, rst, and_5_out);
  Register #(.width(32)) register_6 (.D(multiplexer_1_out), .en(or_6_out), .clk(clk), .Q(R20));  // open: clr
  or or_6 (or_6_out, rst, and_6_out);
  Register #(.width(32)) register_7 (.D(multiplexer_1_out), .en(or_7_out), .clk(clk), .Q(R24));  // open: clr
  or or_7 (or_7_out, rst, and_7_out);
  Register #(.width(32)) register_8 (.D(multiplexer_1_out), .en(or_8_out), .clk(clk), .Q(R28));  // open: clr
  or or_8 (or_8_out, rst, and_8_out);
  Multiplexer #(.select(3), .width(32)) multiplexer_2 (
    .in0({32{1'b0}}), .in1(R4), .in2(R8), .in3(R12), .in4(R16), .in5(R20), .in6(R24), .in7(R28),
    .out(multiplexer_2_out), .sel(Aread0[4:2]));
  Multiplexer #(.select(3), .width(32)) multiplexer_3 (
    .in0({32{1'b0}}), .in1(R4), .in2(R8), .in3(R12), .in4(R16), .in5(R20), .in6(R24), .in7(R28),
    .out(multiplexer_3_out), .sel(Aread1[4:2]));
  and and_9 (and_9_out, decoder_2_out1, decoder_1_out0);
  and and_10 (and_10_out, decoder_2_out1, decoder_1_out1);
  and and_11 (and_11_out, decoder_2_out1, decoder_1_out2);
  and and_12 (and_12_out, decoder_2_out1, decoder_1_out3);
  and and_13 (and_13_out, decoder_2_out1, decoder_1_out4);
  and and_14 (and_14_out, decoder_2_out1, decoder_1_out5);
  and and_15 (and_15_out, decoder_2_out1, decoder_1_out6);
  and and_16 (and_16_out, decoder_2_out1, decoder_1_out7);
  Register #(.width(32)) register_9 (.D(multiplexer_1_out), .en(or_9_out), .clk(clk), .Q(R1));  // open: clr
  or or_9 (or_9_out, rst, and_9_out);
  Register #(.width(32)) register_10 (.D(multiplexer_1_out), .en(or_10_out), .clk(clk), .Q(R5));  // open: clr
  or or_10 (or_10_out, rst, and_10_out);
  Register #(.width(32)) register_11 (.D(multiplexer_1_out), .en(or_11_out), .clk(clk), .Q(R9));  // open: clr
  or or_11 (or_11_out, rst, and_11_out);
  Register #(.width(32)) register_12 (.D(multiplexer_1_out), .en(or_12_out), .clk(clk), .Q(R13));  // open: clr
  or or_12 (or_12_out, rst, and_12_out);
  Register #(.width(32)) register_13 (.D(multiplexer_1_out), .en(or_13_out), .clk(clk), .Q(R17));  // open: clr
  or or_13 (or_13_out, rst, and_13_out);
  Register #(.width(32)) register_14 (.D(multiplexer_1_out), .en(or_14_out), .clk(clk), .Q(R21));  // open: clr
  or or_14 (or_14_out, rst, and_14_out);
  Register #(.width(32)) register_15 (.D(multiplexer_1_out), .en(or_15_out), .clk(clk), .Q(R25));  // open: clr
  or or_15 (or_15_out, rst, and_15_out);
  Register #(.width(32)) register_16 (.D(multiplexer_1_out), .en(or_16_out), .clk(clk), .Q(R29));  // open: clr
  or or_16 (or_16_out, rst, and_16_out);
  Multiplexer #(.select(3), .width(32)) multiplexer_4 (
    .in0(R1), .in1(R5), .in2(R9), .in3(R13), .in4(R17), .in5(R21), .in6(R25), .in7(R29),
    .out(multiplexer_4_out), .sel(Aread0[4:2]));
  Multiplexer #(.select(3), .width(32)) multiplexer_5 (
    .in0(R1), .in1(R5), .in2(R9), .in3(R13), .in4(R17), .in5(R21), .in6(R25), .in7(R29),
    .out(multiplexer_5_out), .sel(Aread1[4:2]));
  Register #(.width(32)) register_17 (.D(multiplexer_1_out), .en(or_17_out), .clk(clk), .Q(R2));  // open: clr
  or or_17 (or_17_out, rst, and_17_out);
  and and_17 (and_17_out, decoder_2_out2, decoder_1_out0);
  Register #(.width(32)) register_18 (.D(multiplexer_1_out), .en(or_18_out), .clk(clk), .Q(R6));  // open: clr
  or or_18 (or_18_out, rst, and_18_out);
  and and_18 (and_18_out, decoder_2_out2, decoder_1_out1);
  Register #(.width(32)) register_19 (.D(multiplexer_1_out), .en(or_19_out), .clk(clk), .Q(R10));  // open: clr
  or or_19 (or_19_out, rst, and_19_out);
  and and_19 (and_19_out, decoder_2_out2, decoder_1_out2);
  Register #(.width(32)) register_20 (.D(multiplexer_1_out), .en(or_20_out), .clk(clk), .Q(R14));  // open: clr
  or or_20 (or_20_out, rst, and_20_out);
  and and_20 (and_20_out, decoder_2_out2, decoder_1_out3);
  Register #(.width(32)) register_21 (.D(multiplexer_1_out), .en(or_21_out), .clk(clk), .Q(R18));  // open: clr
  or or_21 (or_21_out, rst, and_21_out);
  and and_21 (and_21_out, decoder_2_out2, decoder_1_out4);
  Register #(.width(32)) register_22 (.D(multiplexer_1_out), .en(or_22_out), .clk(clk), .Q(R22));  // open: clr
  or or_22 (or_22_out, rst, and_22_out);
  and and_22 (and_22_out, decoder_2_out2, decoder_1_out5);
  Register #(.width(32)) register_23 (.D(multiplexer_1_out), .en(or_23_out), .clk(clk), .Q(R26));  // open: clr
  or or_23 (or_23_out, rst, and_23_out);
  and and_23 (and_23_out, decoder_2_out2, decoder_1_out6);
  Register #(.width(32)) register_24 (.D(multiplexer_1_out), .en(or_24_out), .clk(clk), .Q(R30));  // open: clr
  or or_24 (or_24_out, rst, and_24_out);
  and and_24 (and_24_out, decoder_2_out2, decoder_1_out7);
  Multiplexer #(.select(3), .width(32)) multiplexer_6 (
    .in0(R2), .in1(R6), .in2(R10), .in3(R14), .in4(R18), .in5(R22), .in6(R26), .in7(R30),
    .out(multiplexer_6_out), .sel(Aread0[4:2]));
  Multiplexer #(.select(3), .width(32)) multiplexer_7 (
    .in0(R2), .in1(R6), .in2(R10), .in3(R14), .in4(R18), .in5(R22), .in6(R26), .in7(R30),
    .out(multiplexer_7_out), .sel(Aread1[4:2]));
  Register #(.width(32)) register_25 (.D(multiplexer_1_out), .en(or_25_out), .clk(clk), .Q(R3));  // open: clr
  or or_25 (or_25_out, rst, and_25_out);
  and and_25 (and_25_out, decoder_2_out3, decoder_1_out0);
  Register #(.width(32)) register_26 (.D(multiplexer_1_out), .en(or_26_out), .clk(clk), .Q(R7));  // open: clr
  or or_26 (or_26_out, rst, and_26_out);
  and and_26 (and_26_out, decoder_2_out3, decoder_1_out1);
  Register #(.width(32)) register_27 (.D(multiplexer_1_out), .en(or_27_out), .clk(clk), .Q(R11));  // open: clr
  or or_27 (or_27_out, rst, and_27_out);
  and and_27 (and_27_out, decoder_2_out3, decoder_1_out2);
  Register #(.width(32)) register_28 (.D(multiplexer_1_out), .en(or_28_out), .clk(clk), .Q(R15));  // open: clr
  or or_28 (or_28_out, rst, and_28_out);
  and and_28 (and_28_out, decoder_2_out3, decoder_1_out3);
  Register #(.width(32)) register_29 (.D(multiplexer_1_out), .en(or_29_out), .clk(clk), .Q(R19));  // open: clr
  or or_29 (or_29_out, rst, and_29_out);
  and and_29 (and_29_out, decoder_2_out3, decoder_1_out4);
  Register #(.width(32)) register_30 (.D(multiplexer_1_out), .en(or_30_out), .clk(clk), .Q(R23));  // open: clr
  or or_30 (or_30_out, rst, and_30_out);
  and and_30 (and_30_out, decoder_2_out3, decoder_1_out5);
  Register #(.width(32)) register_31 (.D(multiplexer_1_out), .en(or_31_out), .clk(clk), .Q(R27));  // open: clr
  or or_31 (or_31_out, rst, and_31_out);
  and and_31 (and_31_out, decoder_2_out3, decoder_1_out6);
  Register #(.width(32)) register_32 (.D(multiplexer_1_out), .en(or_32_out), .clk(clk), .Q(R31));  // open: clr
  or or_32 (or_32_out, rst, and_32_out);
  and and_32 (and_32_out, decoder_2_out3, decoder_1_out7);
  Multiplexer #(.select(3), .width(32)) multiplexer_8 (
    .in0(R3), .in1(R7), .in2(R11), .in3(R15), .in4(R19), .in5(R23), .in6(R27), .in7(R31),
    .out(multiplexer_8_out), .sel(Aread0[4:2]));
  Multiplexer #(.select(3), .width(32)) multiplexer_9 (
    .in0(R3), .in1(R7), .in2(R11), .in3(R15), .in4(R19), .in5(R23), .in6(R27), .in7(R31),
    .out(multiplexer_9_out), .sel(Aread1[4:2]));
  Multiplexer #(.select(2), .width(32)) multiplexer_10 (
    .in0(multiplexer_2_out), .in1(multiplexer_4_out), .in2(multiplexer_6_out), .in3(multiplexer_8_out),
    .out(Dread0), .sel(Aread0[1:0]));
  Multiplexer #(.select(2), .width(32)) multiplexer_11 (
    .in0(multiplexer_3_out), .in1(multiplexer_5_out), .in2(multiplexer_7_out), .in3(multiplexer_9_out),
    .out(Dread1), .sel(Aread1[1:0]));

  // Notes on the sheet:
  //   Field Template
endmodule

module jtag_ram8 (
  input  clk,
  input  Jen,
  input  [31:0] Din,
  input  [31:0] Jin,
  input  Wen,
  input  [2:0] Addr,
  output [31:0] Dout,
  output [31:0] Jout
);

  wire decoder_1_out0, decoder_1_out1, decoder_1_out2, decoder_1_out3, decoder_1_out4, decoder_1_out5,
       decoder_1_out6, decoder_1_out7, or_1_out, or_2_out, or_3_out, or_4_out, or_5_out, or_6_out, or_7_out,
       or_8_out;
  wire [31:0] M0, M1, M2, M3, M4, M5, M6, multiplexer_1_out, multiplexer_2_out, multiplexer_3_out,
       multiplexer_4_out, multiplexer_5_out, multiplexer_6_out, multiplexer_7_out, multiplexer_8_out;

  Decoder #(.select(3)) decoder_1 (
    .out0(decoder_1_out0), .out1(decoder_1_out1), .out2(decoder_1_out2), .out3(decoder_1_out3),
    .out4(decoder_1_out4), .out5(decoder_1_out5), .out6(decoder_1_out6), .out7(decoder_1_out7), .sel(Addr),
    .en(Wen));
  Multiplexer #(.width(32)) multiplexer_1 (.in0(Din), .in1(Jin), .out(multiplexer_1_out), .sel(Jen));
  Multiplexer #(.width(32)) multiplexer_2 (.in0(Din), .in1(M0), .out(multiplexer_2_out), .sel(Jen));
  Multiplexer #(.width(32)) multiplexer_3 (.in0(Din), .in1(M1), .out(multiplexer_3_out), .sel(Jen));
  Multiplexer #(.width(32)) multiplexer_4 (.in0(Din), .in1(M2), .out(multiplexer_4_out), .sel(Jen));
  Multiplexer #(.width(32)) multiplexer_5 (.in0(Din), .in1(M3), .out(multiplexer_5_out), .sel(Jen));
  Multiplexer #(.width(32)) multiplexer_6 (.in0(Din), .in1(M4), .out(multiplexer_6_out), .sel(Jen));
  Multiplexer #(.width(32)) multiplexer_7 (.in0(Din), .in1(M5), .out(multiplexer_7_out), .sel(Jen));
  Multiplexer #(.width(32)) multiplexer_8 (.in0(Din), .in1(M6), .out(multiplexer_8_out), .sel(Jen));
  Register #(.width(32)) register_1 (.D(multiplexer_1_out), .en(or_1_out), .clk(clk), .Q(M0));  // open: clr
  or or_1 (or_1_out, Jen, decoder_1_out0);
  Register #(.width(32)) register_2 (.D(multiplexer_2_out), .en(or_2_out), .clk(clk), .Q(M1));  // open: clr
  or or_2 (or_2_out, Jen, decoder_1_out1);
  Register #(.width(32)) register_3 (.D(multiplexer_3_out), .en(or_3_out), .clk(clk), .Q(M2));  // open: clr
  or or_3 (or_3_out, Jen, decoder_1_out2);
  Register #(.width(32)) register_4 (.D(multiplexer_4_out), .en(or_4_out), .clk(clk), .Q(M3));  // open: clr
  or or_4 (or_4_out, Jen, decoder_1_out3);
  Register #(.width(32)) register_5 (.D(multiplexer_5_out), .en(or_5_out), .clk(clk), .Q(M4));  // open: clr
  or or_5 (or_5_out, Jen, decoder_1_out4);
  Register #(.width(32)) register_6 (.D(multiplexer_6_out), .en(or_6_out), .clk(clk), .Q(M5));  // open: clr
  or or_6 (or_6_out, Jen, decoder_1_out5);
  Register #(.width(32)) register_7 (.D(multiplexer_7_out), .en(or_7_out), .clk(clk), .Q(M6));  // open: clr
  or or_7 (or_7_out, Jen, decoder_1_out6);
  Register #(.width(32)) register_8 (.D(multiplexer_8_out), .en(or_8_out), .clk(clk), .Q(Jout));  // open: clr
  or or_8 (or_8_out, Jen, decoder_1_out7);
  Multiplexer #(.select(3), .width(32)) multiplexer_9 (
    .in0(M0), .in1(M1), .in2(M2), .in3(M3), .in4(M4), .in5(M5), .in6(M6), .in7(Jout), .out(Dout), .sel(Addr));

  // Other names for the same wires on the sheet: M7[31:0] = Jout
endmodule

module jtag_ram64 (
  input  clk,
  input  Jen,
  input  [31:0] Din,
  input  [31:0] Jin,
  input  Wen,
  input  [5:0] Addr,
  output [31:0] Dout,
  output [31:0] Jout
);

  wire decoder_1_out0, decoder_1_out1, decoder_1_out2, decoder_1_out3, decoder_1_out4, decoder_1_out5,
       decoder_1_out6, decoder_1_out7;
  wire [31:0] b0_dout, b0_jout, b1_dout, b1_jout, b2_dout, b2_jout, b3_dout, b3_jout, b4_dout, b4_jout,
       b5_dout, b5_jout, b6_dout, b6_jout, b7_dout;

  Decoder #(.select(3)) decoder_1 (
    .out0(decoder_1_out0), .out1(decoder_1_out1), .out2(decoder_1_out2), .out3(decoder_1_out3),
    .out4(decoder_1_out4), .out5(decoder_1_out5), .out6(decoder_1_out6), .out7(decoder_1_out7),
    .sel(Addr[5:3]), .en(Wen));
  jtag_ram8 b0 (
    .clk(clk), .Jen(Jen), .Din(Din), .Jin(Jin), .Wen(decoder_1_out0), .Addr(Addr[2:0]), .Dout(b0_dout),
    .Jout(b0_jout));
  jtag_ram8 b1 (
    .clk(clk), .Jen(Jen), .Din(Din), .Jin(b0_jout), .Wen(decoder_1_out1), .Addr(Addr[2:0]), .Dout(b1_dout),
    .Jout(b1_jout));
  jtag_ram8 b2 (
    .clk(clk), .Jen(Jen), .Din(Din), .Jin(b1_jout), .Wen(decoder_1_out2), .Addr(Addr[2:0]), .Dout(b2_dout),
    .Jout(b2_jout));
  jtag_ram8 b3 (
    .clk(clk), .Jen(Jen), .Din(Din), .Jin(b2_jout), .Wen(decoder_1_out3), .Addr(Addr[2:0]), .Dout(b3_dout),
    .Jout(b3_jout));
  jtag_ram8 b4 (
    .clk(clk), .Jen(Jen), .Din(Din), .Jin(b3_jout), .Wen(decoder_1_out4), .Addr(Addr[2:0]), .Dout(b4_dout),
    .Jout(b4_jout));
  jtag_ram8 b5 (
    .clk(clk), .Jen(Jen), .Din(Din), .Jin(b4_jout), .Wen(decoder_1_out5), .Addr(Addr[2:0]), .Dout(b5_dout),
    .Jout(b5_jout));
  jtag_ram8 b6 (
    .clk(clk), .Jen(Jen), .Din(Din), .Jin(b5_jout), .Wen(decoder_1_out6), .Addr(Addr[2:0]), .Dout(b6_dout),
    .Jout(b6_jout));
  jtag_ram8 b7 (
    .clk(clk), .Jen(Jen), .Din(Din), .Jin(b6_jout), .Wen(decoder_1_out7), .Addr(Addr[2:0]), .Dout(b7_dout),
    .Jout(Jout));
  Multiplexer #(.select(3), .width(32)) multiplexer_1 (
    .in0(b0_dout), .in1(b1_dout), .in2(b2_dout), .in3(b3_dout), .in4(b4_dout), .in5(b5_dout), .in6(b6_dout),
    .in7(b7_dout), .out(Dout), .sel(Addr[5:3]));
endmodule

module jtag_ram512 (
  input  clk,
  input  Jen,
  input  [31:0] Din,
  input  [31:0] Jin,
  input  Wen,
  input  [8:0] Addr,
  output [31:0] Jout,
  output [31:0] Dout
);

  wire decoder_1_out0, decoder_1_out1, decoder_1_out2, decoder_1_out3, decoder_1_out4, decoder_1_out5,
       decoder_1_out6, decoder_1_out7;
  wire [31:0] b0_dout, b0_jout, b1_dout, b1_jout, b2_dout, b2_jout, b3_dout, b3_jout, b4_dout, b4_jout,
       b5_dout, b5_jout, b6_dout, b6_jout, b7_dout;

  Decoder #(.select(3)) decoder_1 (
    .out0(decoder_1_out0), .out1(decoder_1_out1), .out2(decoder_1_out2), .out3(decoder_1_out3),
    .out4(decoder_1_out4), .out5(decoder_1_out5), .out6(decoder_1_out6), .out7(decoder_1_out7),
    .sel(Addr[8:6]), .en(Wen));
  jtag_ram64 b0 (
    .clk(clk), .Jen(Jen), .Din(Din), .Jin(Jin), .Wen(decoder_1_out0), .Addr(Addr[5:0]), .Dout(b0_dout),
    .Jout(b0_jout));
  jtag_ram64 b1 (
    .clk(clk), .Jen(Jen), .Din(Din), .Jin(b0_jout), .Wen(decoder_1_out1), .Addr(Addr[5:0]), .Dout(b1_dout),
    .Jout(b1_jout));
  jtag_ram64 b2 (
    .clk(clk), .Jen(Jen), .Din(Din), .Jin(b1_jout), .Wen(decoder_1_out2), .Addr(Addr[5:0]), .Dout(b2_dout),
    .Jout(b2_jout));
  jtag_ram64 b3 (
    .clk(clk), .Jen(Jen), .Din(Din), .Jin(b2_jout), .Wen(decoder_1_out3), .Addr(Addr[5:0]), .Dout(b3_dout),
    .Jout(b3_jout));
  jtag_ram64 b4 (
    .clk(clk), .Jen(Jen), .Din(Din), .Jin(b3_jout), .Wen(decoder_1_out4), .Addr(Addr[5:0]), .Dout(b4_dout),
    .Jout(b4_jout));
  jtag_ram64 b5 (
    .clk(clk), .Jen(Jen), .Din(Din), .Jin(b4_jout), .Wen(decoder_1_out5), .Addr(Addr[5:0]), .Dout(b5_dout),
    .Jout(b5_jout));
  jtag_ram64 b6 (
    .clk(clk), .Jen(Jen), .Din(Din), .Jin(b5_jout), .Wen(decoder_1_out6), .Addr(Addr[5:0]), .Dout(b6_dout),
    .Jout(b6_jout));
  jtag_ram64 b7 (
    .clk(clk), .Jen(Jen), .Din(Din), .Jin(b6_jout), .Wen(decoder_1_out7), .Addr(Addr[5:0]), .Dout(b7_dout),
    .Jout(Jout));
  Multiplexer #(.select(3), .width(32)) multiplexer_1 (
    .in0(b0_dout), .in1(b1_dout), .in2(b2_dout), .in3(b3_dout), .in4(b4_dout), .in5(b5_dout), .in6(b6_dout),
    .in7(b7_dout), .out(Dout), .sel(Addr[8:6]));
endmodule

module and_func (
  input  [31:0] a,
  input  [31:0] b,
  output [31:0] and_circ
);

  assign and_circ = a & b;  // AND_Gate and_1, 32 bits wide
endmodule

module xor_func (
  input  [31:0] a,
  input  [31:0] b,
  output [31:0] xor_circ
);

  assign xor_circ = a ^ b;  // XOR_Gate xor_1, 32 bits wide
endmodule

module or_func (
  input  [31:0] a,
  input  [31:0] b,
  output [31:0] or_circ
);

  assign or_circ = a | b;  // OR_Gate or_1, 32 bits wide
endmodule

module add_func (
  input  cin,
  input  [31:0] a,
  input  [31:0] b,
  output [31:0] s,
  output cout
);

  wire adder_1_cout, adder_2_cout, adder_3_cout, adder_4_cout, adder_5_cout, adder_6_cout, adder_7_cout,
       adder_8_cout, adder_9_cout, adder_10_cout, adder_11_cout, adder_12_cout, adder_13_cout, adder_14_cout,
       adder_15_cout, multiplexer_2_out, multiplexer_4_out, multiplexer_6_out, multiplexer_8_out,
       multiplexer_10_out, multiplexer_12_out;
  wire [3:0] adder_2_out, adder_3_out, adder_4_out, adder_5_out, adder_6_out, adder_7_out, adder_8_out,
       adder_9_out, adder_10_out, adder_11_out, adder_12_out, adder_13_out, adder_14_out, adder_15_out;

  Adder #(.width(4)) adder_1 (.a(a[3:0]), .b(b[3:0]), .out(s[3:0]), .cin(cin), .cout(adder_1_cout));
  Adder #(.width(4)) adder_2 (.a(a[7:4]), .b(b[7:4]), .out(adder_2_out), .cin(1'b0), .cout(adder_2_cout));
  Adder #(.width(4)) adder_3 (.a(a[7:4]), .b(b[7:4]), .out(adder_3_out), .cin(1'b1), .cout(adder_3_cout));
  Adder #(.width(4)) adder_4 (.a(a[11:8]), .b(b[11:8]), .out(adder_4_out), .cin(1'b0), .cout(adder_4_cout));
  Adder #(.width(4)) adder_5 (.a(a[11:8]), .b(b[11:8]), .out(adder_5_out), .cin(1'b1), .cout(adder_5_cout));
  Adder #(.width(4)) adder_6 (.a(a[15:12]), .b(b[15:12]), .out(adder_6_out), .cin(1'b0), .cout(adder_6_cout));
  Adder #(.width(4)) adder_7 (.a(a[15:12]), .b(b[15:12]), .out(adder_7_out), .cin(1'b1), .cout(adder_7_cout));
  Adder #(.width(4)) adder_8 (.a(a[19:16]), .b(b[19:16]), .out(adder_8_out), .cin(1'b0), .cout(adder_8_cout));
  Adder #(.width(4)) adder_9 (.a(a[19:16]), .b(b[19:16]), .out(adder_9_out), .cin(1'b1), .cout(adder_9_cout));
  Adder #(.width(4)) adder_10 (.a(a[23:20]), .b(b[23:20]), .out(adder_10_out), .cin(1'b0), .cout(adder_10_cout));
  Adder #(.width(4)) adder_11 (.a(a[23:20]), .b(b[23:20]), .out(adder_11_out), .cin(1'b1), .cout(adder_11_cout));
  Adder #(.width(4)) adder_12 (.a(a[27:24]), .b(b[27:24]), .out(adder_12_out), .cin(1'b0), .cout(adder_12_cout));
  Adder #(.width(4)) adder_13 (.a(a[27:24]), .b(b[27:24]), .out(adder_13_out), .cin(1'b1), .cout(adder_13_cout));
  Adder #(.width(4)) adder_14 (.a(a[31:28]), .b(b[31:28]), .out(adder_14_out), .cin(1'b0), .cout(adder_14_cout));
  Adder #(.width(4)) adder_15 (.a(a[31:28]), .b(b[31:28]), .out(adder_15_out), .cin(1'b1), .cout(adder_15_cout));
  Multiplexer #(.width(4)) multiplexer_1 (.in0(adder_2_out), .in1(adder_3_out), .out(s[7:4]), .sel(adder_1_cout));
  Multiplexer multiplexer_2 (.in0(adder_2_cout), .in1(adder_3_cout), .out(multiplexer_2_out), .sel(adder_1_cout));
  Multiplexer #(.width(4)) multiplexer_3 (.in0(adder_4_out), .in1(adder_5_out), .out(s[11:8]), .sel(multiplexer_2_out));
  Multiplexer multiplexer_4 (.in0(adder_4_cout), .in1(adder_5_cout), .out(multiplexer_4_out), .sel(multiplexer_2_out));
  Multiplexer #(.width(4)) multiplexer_5 (
    .in0(adder_6_out), .in1(adder_7_out), .out(s[15:12]), .sel(multiplexer_4_out));
  Multiplexer multiplexer_6 (.in0(adder_6_cout), .in1(adder_7_cout), .out(multiplexer_6_out), .sel(multiplexer_4_out));
  Multiplexer #(.width(4)) multiplexer_7 (
    .in0(adder_8_out), .in1(adder_9_out), .out(s[19:16]), .sel(multiplexer_6_out));
  Multiplexer multiplexer_8 (.in0(adder_8_cout), .in1(adder_9_cout), .out(multiplexer_8_out), .sel(multiplexer_6_out));
  Multiplexer #(.width(4)) multiplexer_9 (
    .in0(adder_10_out), .in1(adder_11_out), .out(s[23:20]), .sel(multiplexer_8_out));
  Multiplexer multiplexer_10 (
    .in0(adder_10_cout), .in1(adder_11_cout), .out(multiplexer_10_out), .sel(multiplexer_8_out));
  Multiplexer #(.width(4)) multiplexer_11 (
    .in0(adder_12_out), .in1(adder_13_out), .out(s[27:24]), .sel(multiplexer_10_out));
  Multiplexer multiplexer_12 (
    .in0(adder_12_cout), .in1(adder_13_cout), .out(multiplexer_12_out), .sel(multiplexer_10_out));
  Multiplexer #(.width(4)) multiplexer_13 (
    .in0(adder_14_out), .in1(adder_15_out), .out(s[31:28]), .sel(multiplexer_12_out));
  Multiplexer multiplexer_14 (.in0(adder_14_cout), .in1(adder_15_cout), .out(cout), .sel(multiplexer_12_out));
endmodule

module sub_func (
  input  [31:0] a,
  input  [31:0] b,
  output [31:0] sub_circ,
  output borrow
);

  wire adder_cout;
  wire [31:0] not_1_out;

  assign not_1_out = ~b;  // NOT_Gate not_1, 32 bits wide
  add_func adder (.cin(1'b1), .a(a), .b(not_1_out), .s(sub_circ), .cout(adder_cout));
  not not_2 (borrow, adder_cout);
endmodule

module sll_func (
  input  [31:0] a,
  input  [31:0] b,
  output [31:0] sll_circ
);

  wire [31:0] multiplexer_1_out, multiplexer_2_out, multiplexer_3_out, multiplexer_4_out;

  Multiplexer #(.width(32)) multiplexer_1 (.in0(a), .in1({a[30:0], 1'b0}), .out(multiplexer_1_out), .sel(b[0]));
  Multiplexer #(.width(32)) multiplexer_2 (
    .in0(multiplexer_1_out), .in1({multiplexer_1_out[29:0], 2'b00}), .out(multiplexer_2_out), .sel(b[1]));
  Multiplexer #(.width(32)) multiplexer_3 (
    .in0(multiplexer_2_out), .in1({multiplexer_2_out[27:0], 4'b0000}), .out(multiplexer_3_out), .sel(b[2]));
  Multiplexer #(.width(32)) multiplexer_4 (
    .in0(multiplexer_3_out), .in1({multiplexer_3_out[23:0], {8{1'b0}}}), .out(multiplexer_4_out), .sel(b[3]));
  Multiplexer #(.width(32)) multiplexer_5 (
    .in0(multiplexer_4_out), .in1({multiplexer_4_out[15:0], {16{1'b0}}}), .out(sll_circ), .sel(b[4]));
endmodule

module srl_func (
  input  [31:0] a,
  input  [3:0] aluop,
  input  [31:0] b,
  output [31:0] outPutshift
);

  wire [1:0] bit_extender_1_out, multiplexer_2_out_2, multiplexer_3_out;
  wire [3:0] bit_extender_2_out, multiplexer_4_out, multiplexer_5_out;
  wire [7:0] bit_extender_3_out, multiplexer_6_out_2, multiplexer_7_out;
  wire [15:0] bit_extender_4_out, multiplexer_9_out;
  wire [23:0] multiplexer_6_out;
  wire [27:0] multiplexer_4_out_2;
  wire [29:0] multiplexer_2_out;
  wire [31:0] multiplexer_8_out;
  wire [31:31] multiplexer_1_out;

  Multiplexer #(.select(2)) multiplexer_1 (
    .in0(1'b0), .in1(a[31]), .in2(a[0]), .out(multiplexer_1_out[31]), .sel({aluop[2], aluop[0]}));  // open: in3
  Multiplexer #(.width(32)) multiplexer_2 (
    .in0(a), .in1({multiplexer_1_out[31], a[31:1]}), .out({multiplexer_2_out, multiplexer_2_out_2}),
    .sel(b[0]));
  assign bit_extender_1_out = {{1{multiplexer_2_out[29]}}, multiplexer_2_out[29]};  // Bit_Extender bit_extender_1
  Multiplexer #(.select(2), .width(2)) multiplexer_3 (
    .in0(2'b00), .in1(bit_extender_1_out), .in2(multiplexer_2_out_2), .out(multiplexer_3_out),
    .sel({aluop[2], aluop[0]}));  // open: in3
  Multiplexer #(.width(32)) multiplexer_4 (
    .in0({multiplexer_2_out, multiplexer_2_out_2}), .in1({multiplexer_3_out, multiplexer_2_out}),
    .out({multiplexer_4_out_2, multiplexer_4_out}), .sel(b[1]));
  assign bit_extender_2_out = {{3{multiplexer_4_out_2[27]}}, multiplexer_4_out_2[27]};  // Bit_Extender bit_extender_2
  Multiplexer #(.select(2), .width(4)) multiplexer_5 (
    .in0(4'b0000), .in1(bit_extender_2_out), .in2(multiplexer_4_out), .out(multiplexer_5_out),
    .sel({aluop[2], aluop[0]}));  // open: in3
  Multiplexer #(.width(32)) multiplexer_6 (
    .in0({multiplexer_4_out_2, multiplexer_4_out}), .in1({multiplexer_5_out, multiplexer_4_out_2}),
    .out({multiplexer_6_out, multiplexer_6_out_2}), .sel(b[2]));
  assign bit_extender_3_out = {{7{multiplexer_6_out[23]}}, multiplexer_6_out[23]};  // Bit_Extender bit_extender_3
  Multiplexer #(.select(2), .width(8)) multiplexer_7 (
    .in0({8{1'b0}}), .in1(bit_extender_3_out), .in2(multiplexer_6_out_2), .out(multiplexer_7_out),
    .sel({aluop[2], aluop[0]}));  // open: in3
  Multiplexer #(.width(32)) multiplexer_8 (
    .in0({multiplexer_6_out, multiplexer_6_out_2}), .in1({multiplexer_7_out, multiplexer_6_out}),
    .out(multiplexer_8_out), .sel(b[3]));
  assign bit_extender_4_out = {{15{multiplexer_8_out[31]}}, multiplexer_8_out[31]};  // Bit_Extender bit_extender_4
  Multiplexer #(.select(2), .width(16)) multiplexer_9 (
    .in0({16{1'b0}}), .in1(bit_extender_4_out), .in2(multiplexer_8_out[15:0]), .out(multiplexer_9_out),
    .sel({aluop[2], aluop[0]}));  // open: in3
  Multiplexer #(.width(32)) multiplexer_10 (
    .in0(multiplexer_8_out), .in1({multiplexer_9_out, multiplexer_8_out[31:16]}), .out(outPutshift),
    .sel(b[4]));
endmodule

module alu (
  input  [31:0] a,
  input  [31:0] b,
  input  [3:0] aluop,
  output [31:0] res
);

  wire sub_circ_borrow;
  wire [0:0] add_circ_cout;
  wire [31:0] add_circ_s, and_circ_and_circ, bit_extender_1_out, multiplexer_2_out, or_circ_or_circ,
       sll_circ_sll_circ, srl_sra_rot_outputshift, sub_circ_sub_circ, xor_circ_xor_circ;

  add_func add_circ (.cin(1'b0), .a(a), .b(b), .s(add_circ_s), .cout(add_circ_cout[0]));
  sub_func sub_circ (.a(a), .b(b), .sub_circ(sub_circ_sub_circ), .borrow(sub_circ_borrow));
  and_func and_circ (.a(a), .b(b), .and_circ(and_circ_and_circ));
  or_func or_circ (.a(a), .b(b), .or_circ(or_circ_or_circ));
  xor_func xor_circ (.a(a), .b(b), .xor_circ(xor_circ_xor_circ));
  sll_func sll_circ (.a(a), .b(b), .sll_circ(sll_circ_sll_circ));
  srl_func srl_sra_rot (.a(a), .aluop(aluop), .b(b), .outPutshift(srl_sra_rot_outputshift));
  assign bit_extender_1_out = {{31{sub_circ_borrow}}, sub_circ_borrow};  // Bit_Extender bit_extender_1
  Multiplexer #(.select(4), .width(32)) multiplexer_1 (
    .in0(add_circ_s), .in1(sub_circ_sub_circ), .in4(and_circ_and_circ), .in5(or_circ_or_circ),
    .in6(xor_circ_xor_circ), .in9(sll_circ_sll_circ), .in10(srl_sra_rot_outputshift),
    .in11(srl_sra_rot_outputshift), .in12(srl_sra_rot_outputshift), .out(res), .sel(aluop));  // open: in2, in3, in7, in8, in13, in14, in15
  Multiplexer #(.select(4), .width(32)) multiplexer_2 (
    .in0({{31{1'b0}}, add_circ_cout[0]}), .in1(bit_extender_1_out), .in4({32{1'b0}}), .in5({32{1'b0}}),
    .in6({32{1'b0}}), .in7({32{1'b0}}), .in8({32{1'b0}}), .in9({32{1'b0}}), .in10({32{1'b0}}),
    .in11({32{1'b0}}), .in12({32{1'b0}}), .in13({32{1'b0}}), .in14({32{1'b0}}), .in15({32{1'b0}}),
    .out(multiplexer_2_out), .sel(aluop));  // open: in2, in3

  // Other names for the same wires on the sheet: res_low[31:0] = res
endmodule

module ALU_CNT (
  input  [1:0] aluop,
  input  [5:0] func,
  output [3:0] alo_control_signal
);

  wire [3:0] multiplexer_1_out, multiplexer_2_out, multiplexer_3_out;

  Multiplexer #(.select(2), .width(4)) multiplexer_1 (
    .in0(4'b1001), .in2(4'b1010), .in3(4'b1011), .out(multiplexer_1_out), .sel(func[1:0]));  // open: in1
  Multiplexer #(.select(3), .width(4)) multiplexer_2 (
    .in0(4'b0000), .in2(4'b0001), .in4(4'b0100), .in5(4'b0101), .in6(4'b0110), .out(multiplexer_2_out),
    .sel(func[2:0]));  // open: in1, in3, in7
  Multiplexer #(.width(4)) multiplexer_3 (
    .in0(multiplexer_1_out), .in1(multiplexer_2_out), .out(multiplexer_3_out), .sel(func[5]));
  Multiplexer #(.select(2), .width(4)) multiplexer_4 (
    .in0(4'b0010), .in1(4'b0000), .in2(multiplexer_3_out), .in3(4'b0000), .out(alo_control_signal),
    .sel(aluop));
endmodule

module CU (
  input  [5:0] opcode,
  output MemtoReg,
  output REGdst,
  output ALUsrc,
  output [1:0] ALUop,
  output RegWrite
);

  wire comparator_1_eq, isnlwsw, not_1_out, not_2_out, not_3_out;
  wire [1:0] adder_1_out, bit_extender_1_out;

  not not_1 (not_1_out, opcode[2]);
  not not_2 (not_2_out, opcode[3]);
  not not_3 (not_3_out, opcode[4]);
  Comparator #(.mode("unsigned"), .width(6)) comparator_1 (
    .a(opcode), .b({6{1'b0}}), .eq(comparator_1_eq));  // open: gt, lt
  nand nand_1 (isnlwsw, opcode[0], opcode[1], not_1_out, opcode[5], not_2_out);
  and and_1 (MemtoReg, opcode[0], opcode[1], not_1_out, not_2_out, not_3_out, opcode[5]);
  not not_4 (ALUsrc, comparator_1_eq);
  assign bit_extender_1_out = {{1{ALUsrc}}, ALUsrc};  // Bit_Extender bit_extender_1
  or or_1 (RegWrite, MemtoReg, comparator_1_eq);
  Multiplexer multiplexer_1 (.in0(isnlwsw), .in1(comparator_1_eq), .out(REGdst), .sel(comparator_1_eq));
  Adder #(.width(2)) adder_1 (.a(bit_extender_1_out), .b(2'b10), .out(adder_1_out));  // open: cin, cout
  Multiplexer #(.width(2)) multiplexer_2 (.in0(2'b00), .in1(adder_1_out), .out(ALUop), .sel(isnlwsw));
endmodule
